// Logisim project Digital-circuit-sim.circ as structural Verilog: 1 circuit, main circuit main
module main (
);

  wire button_1_out, clock_1_out, d_ff_1_q, d_ff_1_qn, d_ff_2_q, d_ff_2_qn, d_ff_3_q, d_ff_3_qn, d_ff_4_q,
       d_ff_4_qn, d_ff_5_q, d_ff_5_qn, d_ff_6_q, d_ff_6_qn, nand_1_out, nand_2_out, nand_3_out, nand_4_out,
       nand_5_out, nand_6_out, not_1_out, not_2_out, not_3_out, not_4_out, not_5_out, not_6_out, not_7_out,
       not_8_out, not_9_out, not_10_out, or_1_out;

  Clock clock_1 (.out(clock_1_out));
  Button button_1 (.out(button_1_out));
  or or_1 (or_1_out, button_1_out, clock_1_out);
  D_Flip_Flop d_ff_1 (.clk(or_1_out), .D(d_ff_3_qn), .Q(d_ff_1_q), .Qn(d_ff_1_qn));  // open: preset, en, reset
  D_Flip_Flop d_ff_2 (
    .clk(or_1_out), .D(d_ff_1_q), .Q(d_ff_2_q), .Qn(d_ff_2_qn), .reset(not_1_out));  // open: preset, en
  not not_1 (not_1_out, nand_1_out);
  nand nand_1 (nand_1_out, d_ff_1_qn, d_ff_3_qn);
  D_Flip_Flop d_ff_3 (.clk(or_1_out), .D(d_ff_2_q), .Q(d_ff_3_q), .Qn(d_ff_3_qn));  // open: preset, en, reset
  nand nand_2 (nand_2_out, nand_1_out, 1'b1);
  nand nand_3 (nand_3_out, d_ff_2_q, d_ff_3_q);
  not not_2 (not_2_out, d_ff_3_q);
  not not_3 (not_3_out, d_ff_2_qn);
  not not_4 (not_4_out, nand_2_out);
  not not_5 (not_5_out, nand_3_out);
  LED led_1 (.in(not_4_out));
  LED led_2 (.in(not_5_out));
  LED led_3 (.in(not_3_out));
  LED led_4 (.in(not_2_out));
  LED led_5 (.in(not_3_out));
  LED led_6 (.in(not_5_out));
  LED led_7 (.in(not_4_out));
  D_Flip_Flop d_ff_4 (.clk(d_ff_3_qn), .D(d_ff_6_qn), .Q(d_ff_4_q), .Qn(d_ff_4_qn));  // open: preset, en, reset
  D_Flip_Flop d_ff_5 (
    .clk(d_ff_3_qn), .D(d_ff_4_q), .Q(d_ff_5_q), .Qn(d_ff_5_qn), .reset(not_6_out));  // open: preset, en
  D_Flip_Flop d_ff_6 (.clk(d_ff_3_qn), .D(d_ff_5_q), .Q(d_ff_6_q), .Qn(d_ff_6_qn));  // open: preset, en, reset
  not not_6 (not_6_out, nand_4_out);
  nand nand_4 (nand_4_out, d_ff_4_qn, d_ff_6_qn);
  nand nand_5 (nand_5_out, nand_4_out, 1'b1);
  nand nand_6 (nand_6_out, d_ff_5_q, d_ff_6_q);
  not not_7 (not_7_out, nand_6_out);
  not not_8 (not_8_out, d_ff_6_q);
  not not_9 (not_9_out, d_ff_5_qn);
  not not_10 (not_10_out, nand_5_out);
  LED led_8 (.in(not_10_out));
  LED led_9 (.in(not_7_out));
  LED led_10 (.in(not_9_out));
  LED led_11 (.in(not_8_out));
  LED led_12 (.in(not_9_out));
  LED led_13 (.in(not_7_out));
  LED led_14 (.in(not_10_out));

  // Notes on the sheet:
  //   ROLL
  //   CLK
endmodule
